// Logisim project TP1 Archi, UAL TITOUAN GAUTIER versionfinal.circ as structural Verilog: 10 circuits, main circuit main
module main (
  input  in_1,
  input  in_2,
  output out_3,
  output out_4
);

  Demi_additionneur demi_additionneur_1 (.A(in_1), .B(in_2), .S(out_3), .C(out_4));
endmodule

module Demi_additionneur (
  input  A,
  input  B,
  output S,
  output C
);

  xor xor_1 (S, A, B);
  and and_1 (C, A, B);
endmodule

module Additionneur_1_bit (
  input  A,
  input  B,
  input  Cin,
  output G,
  output P,
  output S
);

  wire xor_1_out;

  xor xor_1 (xor_1_out, A, B);
  and and_1 (G, A, B);
  or or_1 (P, A, B);
  xor xor_2 (S, xor_1_out, Cin);
endmodule

// r4
module \Unité_de_calcul_anticipé_de_la_retenue  (
  input  Cin,
  input  P1,
  input  G1,
  input  P2,
  input  G2,
  input  P3,
  input  G3,
  input  P4,
  input  G4,
  output r1,
  output r2,
  output r3,
  output r4,
  output rout,
  output out_15,
  output out_16
);

  wire and_1_out, and_2_out, and_3_out, and_5_out, and_6_out, and_7_out, and_8_out, and_9_out, and_10_out,
       and_11_out;

  and and_1 (and_1_out, G1, P2, P3);
  and and_2 (and_2_out, Cin, P1, P2, P3);
  and and_3 (and_3_out, Cin, P1, P2, P3, P4);
  and and_4 (out_16, P1, P2, P3, P4);
  and and_5 (and_5_out, G3, P4);
  and and_6 (and_6_out, G2, P3, P4);
  and and_7 (and_7_out, G1, P2, P3, P4);
  and and_8 (and_8_out, Cin, P1);
  and and_9 (and_9_out, G1, P2);
  and and_10 (and_10_out, Cin, P1, P2);
  and and_11 (and_11_out, G2, P3);
  or or_1 (rout, G4, and_5_out, and_6_out, and_7_out, and_3_out);
  or or_2 (out_15, G4, and_5_out, and_6_out, and_7_out);
  or or_3 (r2, and_8_out, G1);
  or or_4 (r3, G2, and_9_out, and_10_out);
  or or_5 (r4, G3, and_11_out, and_1_out, and_2_out);

  assign r1 = Cin;
endmodule

module \unité_de_calcul_anticipé_non_optimisé  (
  input  Cin,
  input  P1,
  input  G1,
  input  P2,
  input  G2,
  input  P3,
  input  G3,
  input  P4,
  input  G4,
  output r1,
  output r2,
  output r3,
  output r4,
  output rout
);

  wire and_1_out, and_2_out, and_3_out, and_4_out;

  and and_1 (and_1_out, Cin, P1);
  or or_1 (r2, and_1_out, G1);
  and and_2 (and_2_out, r2, P2);
  or or_2 (r3, and_2_out, G2);
  and and_3 (and_3_out, r3, P3);
  or or_3 (r4, and_3_out, G3);
  and and_4 (and_4_out, r4, P4);
  or or_4 (rout, and_4_out, G4);

  assign r1 = Cin;
endmodule

module Additionneur_4bit (
  input  [3:0] B,
  input  [3:0] A,
  input  Cin,
  output [3:0] out_4,
  output Cout,
  output out_6,
  output out_7
);

  wire additionneur_1_bit_1_p, additionneur_1_bit_1_s, additionneur_1_bit_2_p, additionneur_1_bit_2_s,
       additionneur_1_bit_3_p, additionneur_1_bit_3_s, additionneur_1_bit_4_p, additionneur_1_bit_4_s,
       \unité_de_calcul_anticipé_de_la_retenue_1_r1 , \unité_de_calcul_anticipé_de_la_retenue_1_r2 ,
       \unité_de_calcul_anticipé_de_la_retenue_1_r3 , \unité_de_calcul_anticipé_de_la_retenue_1_r4 ;

  Additionneur_1_bit additionneur_1_bit_1 (
    .Cin(\unité_de_calcul_anticipé_de_la_retenue_1_r1 ), .G(out_4[0]), .P(additionneur_1_bit_1_p),
    .S(additionneur_1_bit_1_s), .A(B[0]), .B(A[0]));
  \Unité_de_calcul_anticipé_de_la_retenue  \unité_de_calcul_anticipé_de_la_retenue_1  (
    .Cin(Cin), .P1(additionneur_1_bit_1_s), .G1(additionneur_1_bit_1_p), .P2(additionneur_1_bit_2_s),
    .G2(additionneur_1_bit_2_p), .P3(additionneur_1_bit_3_s), .G3(additionneur_1_bit_3_p),
    .P4(additionneur_1_bit_4_s), .G4(additionneur_1_bit_4_p),
    .r1(\unité_de_calcul_anticipé_de_la_retenue_1_r1 ), .r2(\unité_de_calcul_anticipé_de_la_retenue_1_r2 ),
    .r3(\unité_de_calcul_anticipé_de_la_retenue_1_r3 ), .r4(\unité_de_calcul_anticipé_de_la_retenue_1_r4 ),
    .out_15(out_7), .out_16(out_6), .rout(Cout));
  Additionneur_1_bit additionneur_1_bit_2 (
    .Cin(\unité_de_calcul_anticipé_de_la_retenue_1_r2 ), .G(out_4[1]), .P(additionneur_1_bit_2_p),
    .S(additionneur_1_bit_2_s), .A(B[1]), .B(A[1]));
  Additionneur_1_bit additionneur_1_bit_3 (
    .Cin(\unité_de_calcul_anticipé_de_la_retenue_1_r3 ), .G(out_4[2]), .P(additionneur_1_bit_3_p),
    .S(additionneur_1_bit_3_s), .A(B[2]), .B(A[2]));
  Additionneur_1_bit additionneur_1_bit_4 (
    .Cin(\unité_de_calcul_anticipé_de_la_retenue_1_r4 ), .G(out_4[3]), .P(additionneur_1_bit_4_p),
    .S(additionneur_1_bit_4_s), .A(B[3]), .B(A[3]));
endmodule

module SUPER_PG (
  input  P1,
  input  G1,
  input  P2,
  input  G2,
  input  P3,
  input  G3,
  input  P4,
  input  G4,
  output out_9,
  output out_10
);

  wire and_2_out, and_3_out, and_4_out;

  and and_1 (out_10, P1, P2, P3, G4);
  and and_2 (and_2_out, G3, P4);
  and and_3 (and_3_out, G2, P3, P4);
  and and_4 (and_4_out, G1, P2, P3, P4);
  or or_1 (out_9, G4, and_2_out, and_3_out, and_4_out);
endmodule

module ADDITIONNEUR_16BIT (
  input  [15:0] A,
  input  [15:0] B,
  input  in_3,
  output [15:0] S,
  output out_5,
  output out_6,
  output out_7
);

  wire additionneur_4bit_1_out_6, additionneur_4bit_1_out_7, additionneur_4bit_2_out_6,
       additionneur_4bit_2_out_7, additionneur_4bit_3_out_6, additionneur_4bit_3_out_7,
       additionneur_4bit_4_out_6, additionneur_4bit_4_out_7, \unité_de_calcul_anticipé_de_la_retenue_1_r1 ,
       \unité_de_calcul_anticipé_de_la_retenue_1_r2 , \unité_de_calcul_anticipé_de_la_retenue_1_r3 ,
       \unité_de_calcul_anticipé_de_la_retenue_1_r4 ;

  Additionneur_4bit additionneur_4bit_1 (
    .Cin(\unité_de_calcul_anticipé_de_la_retenue_1_r1 ), .out_6(additionneur_4bit_1_out_6),
    .out_7(additionneur_4bit_1_out_7), .A(A[3:0]), .B(B[3:0]), .out_4(S[3:0]));  // open: Cout
  \Unité_de_calcul_anticipé_de_la_retenue  \unité_de_calcul_anticipé_de_la_retenue_1  (
    .Cin(in_3), .P1(additionneur_4bit_1_out_7), .G1(additionneur_4bit_1_out_6),
    .P2(additionneur_4bit_2_out_7), .G2(additionneur_4bit_2_out_6), .P3(additionneur_4bit_3_out_7),
    .G3(additionneur_4bit_3_out_6), .P4(additionneur_4bit_4_out_7), .G4(additionneur_4bit_4_out_6),
    .r1(\unité_de_calcul_anticipé_de_la_retenue_1_r1 ), .r2(\unité_de_calcul_anticipé_de_la_retenue_1_r2 ),
    .r3(\unité_de_calcul_anticipé_de_la_retenue_1_r3 ), .r4(\unité_de_calcul_anticipé_de_la_retenue_1_r4 ),
    .out_15(out_7), .out_16(out_6), .rout(out_5));
  Additionneur_4bit additionneur_4bit_2 (
    .Cin(\unité_de_calcul_anticipé_de_la_retenue_1_r2 ), .out_6(additionneur_4bit_2_out_6),
    .out_7(additionneur_4bit_2_out_7), .A(A[7:4]), .B(B[7:4]), .out_4(S[7:4]));  // open: Cout
  Additionneur_4bit additionneur_4bit_3 (
    .Cin(\unité_de_calcul_anticipé_de_la_retenue_1_r3 ), .out_6(additionneur_4bit_3_out_6),
    .out_7(additionneur_4bit_3_out_7), .A(A[11:8]), .B(B[11:8]), .out_4(S[11:8]));  // open: Cout
  Additionneur_4bit additionneur_4bit_4 (
    .Cin(\unité_de_calcul_anticipé_de_la_retenue_1_r4 ), .out_6(additionneur_4bit_4_out_6),
    .out_7(additionneur_4bit_4_out_7), .A(A[15:12]), .B(B[15:12]), .out_4(S[15:12]));  // open: Cout
endmodule

module MULTI (
  input  [15:0] A,
  input  [15:0] B,
  input  in_3,
  output [15:0] S,
  output out_5,
  output out_6,
  output out_7
);

  wire [15:0] multiplexer_1_out, not_1_out;

  assign not_1_out = ~B;  // NOT_Gate not_1, 16 bits wide
  Multiplexer #(.width(16), .enable("false")) multiplexer_1 (
    .in0(B), .in1(not_1_out), .out(multiplexer_1_out), .sel(in_3));
  ADDITIONNEUR_16BIT additionneur_16bit_1 (
    .A(multiplexer_1_out), .B(A), .in_3(in_3), .S(S), .out_5(out_5), .out_6(out_6), .out_7(out_7));
endmodule

module UAL (
  input  [15:0] A,
  input  [15:0] B,
  input  [2:0] in_3,
  output [15:0] out_4
);

  wire [15:0] additionneur_16bit_1_s, additionneur_16bit_2_s, and_1_out, not_1_out, not_2_out, or_1_out,
       shifter_1_out, xor_1_out;

  assign not_1_out = ~A;  // NOT_Gate not_1, 16 bits wide
  assign not_2_out = ~A;  // NOT_Gate not_2, 16 bits wide
  assign and_1_out = A & B;  // AND_Gate and_1, 16 bits wide
  assign or_1_out = A | B;  // OR_Gate or_1, 16 bits wide
  assign xor_1_out = A ^ B;  // XOR_Gate xor_1, 16 bits wide
  Shifter #(.width(16)) shifter_1 (.in(A), .\dist (4'b1111), .out(shifter_1_out));
  Shifter #(.width(16), .shift("ar")) shifter_2 (.in(A), .\dist (4'b1111), .out(shifter_1_out));
  ADDITIONNEUR_16BIT additionneur_16bit_1 (
    .A(A), .B(B), .S(additionneur_16bit_1_s));  // open: in_3, out_5, out_6, out_7
  ADDITIONNEUR_16BIT additionneur_16bit_2 (
    .A(not_1_out), .B(B), .S(additionneur_16bit_2_s));  // open: in_3, out_5, out_6, out_7
  Multiplexer #(.select(3), .width(16), .enable("false")) multiplexer_1 (
    .in0(additionneur_16bit_1_s), .in1(additionneur_16bit_2_s), .in2(not_2_out), .in3(and_1_out),
    .in4(or_1_out), .in5(xor_1_out), .in6(shifter_1_out), .in7(shifter_1_out), .out(out_4), .sel(in_3));
endmodule
