// Logisim project TP Archi TITOUAN GAUTIER.circ as structural Verilog: 6 circuits, main circuit main
module main (
  input  in_1,
  input  in_2,
  output out_3,
  output out_4
);

  Demi_additionneur demi_additionneur_1 (.A(in_1), .B(in_2), .S(out_3), .C(out_4));
endmodule

module Demi_additionneur (
  input  A,
  input  B,
  output S,
  output C
);

  xor xor_1 (S, A, B);
  and and_1 (C, A, B);
endmodule

module Additionneur_1_bit (
  input  A,
  input  B,
  input  Cin,
  output G,
  output P,
  output S
);

  wire xor_1_out;

  xor xor_1 (xor_1_out, A, B);
  and and_1 (G, A, B);
  or or_1 (P, A, B);
  xor xor_2 (S, xor_1_out, Cin);
endmodule

// r4
module \Unité_de_calcul_anticipé_de_la_retenue  (
  input  Cin,
  input  P1,
  input  G1,
  input  P2,
  input  G2,
  input  P3,
  input  G3,
  input  P4,
  input  G4,
  output r1,
  output r2,
  output r3,
  output r4,
  output rout
);

  wire and_1_out, and_2_out, and_3_out, and_4_out, and_5_out, and_6_out, and_7_out, and_8_out, and_9_out,
       and_10_out;

  and and_1 (and_1_out, G1, P2, P3);
  and and_2 (and_2_out, Cin, P1, P2, P3);
  and and_3 (and_3_out, G3, P4);
  and and_4 (and_4_out, G2, P3, P4);
  and and_5 (and_5_out, G1, P2, P3, P4);
  and and_6 (and_6_out, Cin, P1, P2, P3, P4);
  and and_7 (and_7_out, Cin, P1);
  and and_8 (and_8_out, G1, P2);
  and and_9 (and_9_out, Cin, P1, P2);
  and and_10 (and_10_out, G2, P3);
  or or_1 (r2, and_7_out, G1);
  or or_2 (r3, G2, and_8_out, and_9_out);
  or or_3 (r4, G3, and_10_out, and_1_out, and_2_out);
  or or_4 (rout, G4, and_3_out, and_4_out, and_5_out, and_6_out);

  assign r1 = Cin;
endmodule

module \unité_de_calcul_anticipé_non_optimisé  (
  input  Cin,
  input  P1,
  input  G1,
  input  P2,
  input  G2,
  input  P3,
  input  G3,
  input  P4,
  input  G4,
  output r1,
  output r2,
  output r3,
  output r4,
  output rout
);

  wire and_1_out, and_2_out, and_3_out, and_4_out;

  and and_1 (and_1_out, Cin, P1);
  or or_1 (r2, and_1_out, G1);
  and and_2 (and_2_out, r2, P2);
  or or_2 (r3, and_2_out, G2);
  and and_3 (and_3_out, r3, P3);
  or or_3 (r4, and_3_out, G3);
  and and_4 (and_4_out, r4, P4);
  or or_4 (rout, and_4_out, G4);

  assign r1 = Cin;
endmodule

module Additionneur_4bit (
  input  in_1,
  input  in_2,
  input  in_3,
  input  in_4,
  input  in_5,
  input  in_6,
  input  in_7,
  input  in_8,
  input  in_9,
  output out_10,
  output out_11,
  output out_12,
  output out_13,
  output out_14
);

  wire additionneur_1_bit_1_p, additionneur_1_bit_1_s, additionneur_1_bit_2_p, additionneur_1_bit_2_s,
       additionneur_1_bit_3_p, additionneur_1_bit_3_s, additionneur_1_bit_4_p, additionneur_1_bit_4_s,
       \unité_de_calcul_anticipé_de_la_retenue_1_r1 , \unité_de_calcul_anticipé_de_la_retenue_1_r2 ,
       \unité_de_calcul_anticipé_de_la_retenue_1_r3 , \unité_de_calcul_anticipé_de_la_retenue_1_r4 ;

  Additionneur_1_bit additionneur_1_bit_1 (
    .Cin(\unité_de_calcul_anticipé_de_la_retenue_1_r1 ), .G(out_10), .P(additionneur_1_bit_1_p),
    .S(additionneur_1_bit_1_s), .A(in_2), .B(in_1));
  \Unité_de_calcul_anticipé_de_la_retenue  \unité_de_calcul_anticipé_de_la_retenue_1  (
    .Cin(in_9), .P1(additionneur_1_bit_1_s), .G1(additionneur_1_bit_1_p), .P2(additionneur_1_bit_2_s),
    .G2(additionneur_1_bit_2_p), .P3(additionneur_1_bit_3_s), .G3(additionneur_1_bit_3_p),
    .P4(additionneur_1_bit_4_s), .G4(additionneur_1_bit_4_p),
    .r1(\unité_de_calcul_anticipé_de_la_retenue_1_r1 ), .r2(\unité_de_calcul_anticipé_de_la_retenue_1_r2 ),
    .r3(\unité_de_calcul_anticipé_de_la_retenue_1_r3 ), .r4(\unité_de_calcul_anticipé_de_la_retenue_1_r4 ),
    .rout(out_14));
  Additionneur_1_bit additionneur_1_bit_2 (
    .Cin(\unité_de_calcul_anticipé_de_la_retenue_1_r2 ), .G(out_11), .P(additionneur_1_bit_2_p),
    .S(additionneur_1_bit_2_s), .A(in_4), .B(in_3));
  Additionneur_1_bit additionneur_1_bit_3 (
    .Cin(\unité_de_calcul_anticipé_de_la_retenue_1_r3 ), .G(out_12), .P(additionneur_1_bit_3_p),
    .S(additionneur_1_bit_3_s), .A(in_6), .B(in_5));
  Additionneur_1_bit additionneur_1_bit_4 (
    .Cin(\unité_de_calcul_anticipé_de_la_retenue_1_r4 ), .G(out_13), .P(additionneur_1_bit_4_p),
    .S(additionneur_1_bit_4_s), .A(in_8), .B(in_7));
endmodule
