// Logisim project nanop.circ as structural Verilog: 1 circuit, main circuit main
// Z
module main (
);

  wire and_2_out, branch_if_N, branch_if_Z, clk, do_branch, e_wr_A, e_wr_CCR, is_ba, is_branch, is_sub, N,
       nor_1_out, reset, rom_3_data, sel_A_src, sel_ext_op, sel_op0, sel_op1, store, write_A, write_CCR, Z;
  wire [3:0] rom_1_data;
  wire [7:0] A_q, adder_1_out, bit_extender_1_out, multiplexer_1_out, multiplexer_2_out, multiplexer_3_out,
       multiplexer_4_out, multiplexer_5_out, multiplexer_6_out, not_1_out, PC_q, ram_1_data, result;
  wire [7:4] rom_1_data_2;

  Adder adder_1 (.a(PC_q), .b(8'h1), .out(adder_1_out), .cin(1'b0));  // open: cout
  Multiplexer #(.width(8), .enable("false")) multiplexer_1 (
    .in0(result), .in1(multiplexer_2_out), .out(multiplexer_1_out), .sel(sel_A_src));
  Multiplexer #(.width(8), .enable("false")) multiplexer_2 (
    .in0(ram_1_data), .in1(bit_extender_1_out), .out(multiplexer_2_out), .sel(sel_ext_op));
  Register A (.D(multiplexer_1_out), .Q(A_q), .clk(write_A), .clr(reset));  // open: en
  // Probe on PC_q
  Multiplexer #(.width(8), .enable("false")) multiplexer_3 (
    .in0(adder_1_out), .in1(result), .out(multiplexer_3_out), .sel(do_branch));
  Register #(.trigger("falling")) PC (.D(multiplexer_3_out), .Q(PC_q), .clk(clk), .clr(reset));  // open: en
  Clock clock_1 (.out(clk));
  // Probe on A_q
  Button u_reset (.out(reset));
  // Probe on multiplexer_4_out
  Multiplexer #(.width(8), .enable("false")) multiplexer_4 (
    .in0(A_q), .in1(PC_q), .out(multiplexer_4_out), .sel(sel_op0));
  ROM rom_1 (.addr(PC_q), .data({rom_1_data_2, rom_1_data}));  // open: sel
  // Probe on ram_1_data
  RAM #(.addrWidth(4), .bus("separate")) ram_1 (
    .addr(rom_1_data), .din(A_q), .data(ram_1_data), .str(store), .sel(1'b1), .clk(clk), .ld(1'b1), .clr(1'b0));
  // Probe on bit_extender_1_out
  Multiplexer #(.width(8), .enable("false")) multiplexer_5 (
    .in0(ram_1_data), .in1(bit_extender_1_out), .out(multiplexer_5_out), .sel(sel_op1));
  assign bit_extender_1_out = {{4{rom_1_data[3]}}, rom_1_data};  // Bit_Extender bit_extender_1
  and and_1 (write_A, e_wr_A, clk);
  // Probe on multiplexer_5_out
  Multiplexer #(.width(8), .enable("false")) multiplexer_6 (
    .in0(multiplexer_5_out), .in1(not_1_out), .out(multiplexer_6_out), .sel(is_sub));
  assign not_1_out = ~multiplexer_5_out;  // NOT_Gate not_1, 8 bits wide
  ROM #(.addrWidth(4), .dataWidth(12)) rom_2 (
    .addr(rom_1_data_2),
    .data({sel_ext_op, store, e_wr_CCR, e_wr_A, sel_op1, is_sub, sel_op0, sel_A_src, is_ba, branch_if_N, branch_if_Z, is_branch}));  // open: sel
  Adder adder_2 (.a(multiplexer_4_out), .b(multiplexer_6_out), .out(result), .cin(is_sub));  // open: cout
  // Probe on result
  ROM #(.addrWidth(4), .dataWidth(1)) rom_3 (.addr({branch_if_Z, branch_if_N, Z, N}), .data(rom_3_data));  // open: sel
  nor nor_1 (nor_1_out, result[0], result[1], result[2], result[3], result[4], result[5], result[6], result[7]);
  and and_2 (and_2_out, is_branch, rom_3_data);
  and and_3 (write_CCR, e_wr_CCR, clk);
  Register #(.width(1)) u_Z (.D(nor_1_out), .Q(Z), .clk(write_CCR), .clr(reset));  // open: en
  Register #(.width(1)) u_N (.D(result[7]), .Q(N), .clk(write_CCR), .clr(reset));  // open: en
  or or_1 (do_branch, is_ba, and_2_out);

  // Notes on the sheet:
  //   contents of rom_1 (hex, n*v repeats v):
  //   40 81 62 fe
  //   contents of rom_2 (hex, n*v repeats v):
  //   300 340 0 240 110 0 400 0 380 a1 a5 2c0 910 a3 a7 a9
  //   contents of rom_3 (hex, n*v repeats v):
  //   0 1 0 1 1 0 1 0 0 0 4*1
endmodule
